// Logisim project CPU.circ as structural Verilog: 5 circuits, main circuit main
module main (
);

  wire ADD_0, AND_0, and_1_out, clk, d_ff_1_q, HALT_0, JUMP_0, JUMPIF_0, JUMPIF_1, LOAD_0, load_code,
       n7_segment_display_1_p1, n7_segment_display_2_p1, n7_segment_display_3_p1, NAND_0, NOR_0, not_1_out,
       not_2_out, not_3_out, not_4_out, not_5_out, not_6_out, not_7_out, not_8_out, OR_0, R, R1, R2, R3, R4,
       R5, R6, R7, reset_clk, reset_code, reset_registre, run_clock, SUB_0, XNOR_0, XOR_0;
  wire [3:0] multiplexer_1_out, opp, read, read1, read2, write;
  wire [4:0] clock_maison_1_value_clk;
  wire [7:0] LEC1, LEC2, multiplexer_2_out, multiplexer_3_out, OUTPUT_ALU;

  ALU_maison alu_maison_1 (.INPUT_A(LEC1), .INPUT_B(LEC2), .opp(opp), .OUTPUT_ALU(OUTPUT_ALU));
  not not_1 (not_1_out, OUTPUT_ALU[0]);
  not not_2 (not_2_out, OUTPUT_ALU[1]);
  not not_3 (not_3_out, OUTPUT_ALU[2]);
  not not_4 (not_4_out, OUTPUT_ALU[3]);
  not not_5 (not_5_out, OUTPUT_ALU[4]);
  not not_6 (not_6_out, OUTPUT_ALU[5]);
  not not_7 (not_7_out, OUTPUT_ALU[6]);
  not not_8 (not_8_out, OUTPUT_ALU[7]);
  Multiplexer #(.width(4)) multiplexer_1 (.in0(read1), .in1(read), .out(multiplexer_1_out), .sel(R));
  Multiplexer #(.width(8)) multiplexer_2 (
    .in0(OUTPUT_ALU), .in1({read2, read1}), .out(multiplexer_2_out), .sel(LOAD_0));
  Multiplexer #(.select(2), .width(8)) multiplexer_3 (
    .in0(OUTPUT_ALU), .in1({read2, read1}), .in2({read2, read1}), .out(multiplexer_3_out),
    .sel({JUMPIF_1, JUMP_0}));  // open: in3
  D_Flip_Flop d_ff_1 (.D(and_1_out), .clk(clk), .Q(d_ff_1_q), .reset(reset_clk));  // open: Qn, preset
  and and_1 (and_1_out, not_1_out, not_2_out, not_3_out, not_4_out, not_5_out, not_6_out, not_7_out, not_8_out);
  and and_2 (JUMPIF_1, JUMPIF_0, d_ff_1_q);
  registre_cpu registre_cpu_1 (
    .WRITE(write), .READ1(multiplexer_1_out), .READ2(read2), .bit_in(multiplexer_2_out), .clk(clk),
    .reset(reset_registre), .LEC1(LEC1), .LEC2(LEC2));
  clock_maison clock_maison_1 (
    .clk(clk), .reset(reset_clk), .run(run_clock), .halt_0(HALT_0), .jumpif_0(JUMPIF_1), .jump_0(JUMP_0),
    .bit_in(multiplexer_3_out), .value_clk(clock_maison_1_value_clk));
  Decoder #(.select(4)) decoder_1 (
    .out0(ADD_0), .out1(OR_0), .out2(XNOR_0), .out3(NAND_0), .out4(NOR_0), .out5(XOR_0), .out6(AND_0),
    .out7(SUB_0), .out8(LOAD_0), .out9(HALT_0), .out10(JUMP_0), .out11(JUMPIF_0), .sel(opp));  // open: out12, out13, out14, out15, en
  registre_code registre_code_1 (
    .load(load_code), .reset(reset_code), .value_clk(clock_maison_1_value_clk),
    .output_code({read1, read2, write, opp}));
  Button u_reset_clk (.out(reset_clk));
  Button u_reset_registre (.out(reset_registre));
  Button u_reset_code (.out(reset_code));
  Button u_load_code (.out(load_code));
  Button u_run_clock (.out(run_clock));
  Clock clock_1 (.out(clk));
  // BCD_to_7_Segment_decoder bcd_to_7_segment_decoder_1: pin names not known
  // _7_Segment_Display 7_segment_display_1: pin names not known; wires that end beside it: n7_segment_display_1_p1, n7_segment_display_1_p1
  // Binary_to_BCD_converter #(.binvalue(8)) binary_to_bcd_converter_1: pin names not known; wires that end beside it: LEC1
  LED led_1 (.in(clk));
  // BCD_to_7_Segment_decoder bcd_to_7_segment_decoder_2: pin names not known
  // BCD_to_7_Segment_decoder bcd_to_7_segment_decoder_3: pin names not known
  // _7_Segment_Display 7_segment_display_2: pin names not known; wires that end beside it: n7_segment_display_2_p1, n7_segment_display_2_p1
  // _7_Segment_Display 7_segment_display_3: pin names not known; wires that end beside it: n7_segment_display_3_p1, n7_segment_display_3_p1
  // DipSwitch #(.number(1)) READ_R1: pin names not known; wires that end beside it: R1
  // DipSwitch #(.number(1)) READ_R2: pin names not known; wires that end beside it: R2
  // DipSwitch #(.number(1)) READ_R3: pin names not known; wires that end beside it: R3
  // DipSwitch #(.number(1)) READ_R4: pin names not known; wires that end beside it: R4
  // DipSwitch #(.number(1)) READ_R5: pin names not known; wires that end beside it: R5
  // DipSwitch #(.number(1)) READ_R6: pin names not known; wires that end beside it: R6
  // DipSwitch #(.number(1)) READ_R7: pin names not known; wires that end beside it: R7
  assign read = R1 ? 4'b0001 : 4'bz;  // Controlled_Buffer controlled_buffer_1
  assign read = R4 ? 4'b0100 : 4'bz;  // Controlled_Buffer controlled_buffer_2
  assign read = R6 ? 4'b0110 : 4'bz;  // Controlled_Buffer controlled_buffer_3
  assign read = R2 ? 4'b0010 : 4'bz;  // Controlled_Buffer controlled_buffer_4
  assign read = R5 ? 4'b0101 : 4'bz;  // Controlled_Buffer controlled_buffer_5
  assign read = R7 ? 4'b0111 : 4'bz;  // Controlled_Buffer controlled_buffer_6
  assign read = R3 ? 4'b0011 : 4'bz;  // Controlled_Buffer controlled_buffer_7
  or or_1 (R, R1, R2, R3, R4, R5, R6, R7);
endmodule

module ALU_maison (
  input  [3:0] opp,
  input  [7:0] INPUT_A,
  input  [7:0] INPUT_B,
  output [7:0] OUTPUT_ALU
);

  wire and_2_out, and_3_out, and_4_out, and_5_out, and_6_out, and_7_out, and_8_out, and_9_out, and_10_out,
       and_11_out, and_12_out, and_13_out, and_14_out, and_15_out, and_16_out, and_17_out, and_18_out,
       and_19_out, and_20_out, and_21_out, and_22_out, and_23_out, and_24_out, and_25_out, and_26_out,
       and_27_out, and_28_out, and_29_out, and_30_out, and_31_out, and_32_out, and_33_out, not_1_out,
       not_2_out, not_3_out, not_4_out, not_5_out, not_6_out, not_7_out, not_8_out, or_9_out, or_17_out, R0,
       R0b, R1, R1b, R2, R2b, R3, R3b, R4, R4b, R5, R5b, R6, R6b, xor_2_out, xor_3_out, xor_4_out, xor_5_out,
       xor_6_out, xor_7_out, xor_8_out, xor_9_out, xor_18_out, xor_19_out, xor_20_out, xor_21_out,
       xor_22_out, xor_23_out, xor_24_out, xor_25_out;
  wire [7:0] S_ADD, S_AND, S_NAND, S_NOR, S_NXOR, S_OR, S_SUB, S_XOR;

  Multiplexer #(.select(4), .width(8)) multiplexer_1 (
    .in0(S_ADD), .in1(S_OR), .in2(S_NXOR), .in3(S_NAND), .in4(S_NOR), .in5(S_XOR), .in6(S_AND), .in7(S_SUB),
    .out(OUTPUT_ALU), .sel(opp));  // open: in8, in9, in10, in11, in12, in13, in14, in15
  assign S_AND = INPUT_A & INPUT_B;  // AND_Gate and_1, 8 bits wide
  assign S_NAND = ~(INPUT_A & INPUT_B);  // NAND_Gate nand_1, 8 bits wide
  assign S_OR = INPUT_A | INPUT_B;  // OR_Gate or_1, 8 bits wide
  assign S_NOR = ~(INPUT_A | INPUT_B);  // NOR_Gate nor_1, 8 bits wide
  assign S_XOR = INPUT_A ^ INPUT_B;  // XOR_Gate xor_1, 8 bits wide
  assign S_NXOR = ~(INPUT_A ^ INPUT_B);  // XNOR_Gate xnor_1, 8 bits wide
  xor xor_2 (xor_2_out, INPUT_A[0], INPUT_B[0]);
  xor xor_3 (xor_3_out, INPUT_A[1], INPUT_B[1]);
  xor xor_4 (xor_4_out, INPUT_A[2], INPUT_B[2]);
  xor xor_5 (xor_5_out, INPUT_A[3], INPUT_B[3]);
  xor xor_6 (xor_6_out, INPUT_A[4], INPUT_B[4]);
  xor xor_7 (xor_7_out, INPUT_A[5], INPUT_B[5]);
  xor xor_8 (xor_8_out, INPUT_A[6], INPUT_B[6]);
  xor xor_9 (xor_9_out, INPUT_A[7], INPUT_B[7]);
  and and_2 (and_2_out, 1'b0, xor_2_out);
  and and_3 (and_3_out, INPUT_B[0], INPUT_A[0]);
  and and_4 (and_4_out, R0, xor_3_out);
  and and_5 (and_5_out, INPUT_B[1], INPUT_A[1]);
  and and_6 (and_6_out, R1, xor_4_out);
  and and_7 (and_7_out, INPUT_B[2], INPUT_A[2]);
  and and_8 (and_8_out, R2, xor_5_out);
  and and_9 (and_9_out, INPUT_B[3], INPUT_A[3]);
  and and_10 (and_10_out, R3, xor_6_out);
  and and_11 (and_11_out, INPUT_B[4], INPUT_A[4]);
  and and_12 (and_12_out, R4, xor_7_out);
  and and_13 (and_13_out, INPUT_B[5], INPUT_A[5]);
  and and_14 (and_14_out, R5, xor_8_out);
  and and_15 (and_15_out, INPUT_B[6], INPUT_A[6]);
  and and_16 (and_16_out, R6, xor_9_out);
  and and_17 (and_17_out, INPUT_B[7], INPUT_A[7]);
  xor xor_10 (S_ADD[0], xor_2_out, 1'b0);
  or or_2 (R0, and_2_out, and_3_out);
  xor xor_11 (S_ADD[1], xor_3_out, R0);
  or or_3 (R1, and_4_out, and_5_out);
  xor xor_12 (S_ADD[2], xor_4_out, R1);
  or or_4 (R2, and_6_out, and_7_out);
  xor xor_13 (S_ADD[3], xor_5_out, R2);
  or or_5 (R3, and_8_out, and_9_out);
  xor xor_14 (S_ADD[4], xor_6_out, R3);
  or or_6 (R4, and_10_out, and_11_out);
  xor xor_15 (S_ADD[5], xor_7_out, R4);
  or or_7 (R5, and_12_out, and_13_out);
  xor xor_16 (S_ADD[6], xor_8_out, R5);
  or or_8 (R6, and_14_out, and_15_out);
  xor xor_17 (S_ADD[7], xor_9_out, R6);
  or or_9 (or_9_out, and_16_out, and_17_out);
  LED led_1 (.in(or_9_out));
  not not_1 (not_1_out, INPUT_B[0]);
  not not_2 (not_2_out, INPUT_B[1]);
  not not_3 (not_3_out, INPUT_B[2]);
  not not_4 (not_4_out, INPUT_B[3]);
  not not_5 (not_5_out, INPUT_B[4]);
  not not_6 (not_6_out, INPUT_B[5]);
  not not_7 (not_7_out, INPUT_B[6]);
  not not_8 (not_8_out, INPUT_B[7]);
  xor xor_18 (xor_18_out, INPUT_A[0], not_1_out);
  xor xor_19 (xor_19_out, INPUT_A[1], not_2_out);
  xor xor_20 (xor_20_out, INPUT_A[2], not_3_out);
  xor xor_21 (xor_21_out, INPUT_A[3], not_4_out);
  xor xor_22 (xor_22_out, INPUT_A[4], not_5_out);
  xor xor_23 (xor_23_out, INPUT_A[5], not_6_out);
  xor xor_24 (xor_24_out, INPUT_A[6], not_7_out);
  xor xor_25 (xor_25_out, INPUT_A[7], not_8_out);
  xor xor_26 (S_SUB[0], xor_18_out, 1'b1);
  and and_18 (and_18_out, 1'b1, xor_18_out);
  and and_19 (and_19_out, not_1_out, INPUT_A[0]);
  xor xor_27 (S_SUB[1], xor_19_out, R0b);
  and and_20 (and_20_out, R0b, xor_19_out);
  and and_21 (and_21_out, not_2_out, INPUT_A[1]);
  xor xor_28 (S_SUB[2], xor_20_out, R1b);
  and and_22 (and_22_out, R1b, xor_20_out);
  and and_23 (and_23_out, not_3_out, INPUT_A[2]);
  xor xor_29 (S_SUB[3], xor_21_out, R2b);
  and and_24 (and_24_out, R2b, xor_21_out);
  and and_25 (and_25_out, not_4_out, INPUT_A[3]);
  xor xor_30 (S_SUB[4], xor_22_out, R3b);
  and and_26 (and_26_out, R3b, xor_22_out);
  and and_27 (and_27_out, not_5_out, INPUT_A[4]);
  xor xor_31 (S_SUB[5], xor_23_out, R4b);
  and and_28 (and_28_out, R4b, xor_23_out);
  and and_29 (and_29_out, not_6_out, INPUT_A[5]);
  xor xor_32 (S_SUB[6], xor_24_out, R5b);
  and and_30 (and_30_out, R5b, xor_24_out);
  and and_31 (and_31_out, not_7_out, INPUT_A[6]);
  xor xor_33 (S_SUB[7], xor_25_out, R6b);
  and and_32 (and_32_out, R6b, xor_25_out);
  and and_33 (and_33_out, not_8_out, INPUT_A[7]);
  or or_10 (R0b, and_18_out, and_19_out);
  or or_11 (R1b, and_20_out, and_21_out);
  or or_12 (R2b, and_22_out, and_23_out);
  or or_13 (R3b, and_24_out, and_25_out);
  or or_14 (R4b, and_26_out, and_27_out);
  or or_15 (R5b, and_28_out, and_29_out);
  or or_16 (R6b, and_30_out, and_31_out);
  or or_17 (or_17_out, and_32_out, and_33_out);
  LED led_2 (.in(or_17_out));

  // Other names for the same wires on the sheet: N1[7:0] = INPUT_A; N1_0 = INPUT_A[0]; N1_1 = INPUT_A[1];
  //   N1_2 = INPUT_A[2]; N1_3 = INPUT_A[3]; N1_4 = INPUT_A[4]; N1_5 = INPUT_A[5]; N1_6 = INPUT_A[6];
  //   N1_7 = INPUT_A[7]; N2[7:0] = INPUT_B; N2_0 = INPUT_B[0]; N2_1 = INPUT_B[1]; N2_2 = INPUT_B[2];
  //   N2_3 = INPUT_B[3]; N2_4 = INPUT_B[4]; N2_5 = INPUT_B[5]; N2_6 = INPUT_B[6]; N2_7 = INPUT_B[7]
endmodule

module registre_cpu (
  input  [3:0] WRITE,
  input  [3:0] READ1,
  input  [3:0] READ2,
  input  [7:0] bit_in,
  input  clk,
  input  reset,
  output [7:0] LEC1,
  output [7:0] LEC2
);

  wire E1, E2, E3, E4, E5, E6, E7;
  wire [7:0] L1_1, L1_2, L1_3, L1_4, L1_5, L1_6, L1_7, L2_1, L2_2, L2_3, L2_4, L2_5, L2_6, L2_7;

  Register register_1 (.D(bit_in), .en(E1), .clk(clk), .Q(L1_1), .clr(reset));
  Register register_2 (.D(bit_in), .en(E2), .clk(clk), .Q(L1_2), .clr(reset));
  Register register_3 (.D(bit_in), .en(E3), .clk(clk), .Q(L1_3), .clr(reset));
  Register register_4 (.D(bit_in), .en(E4), .clk(clk), .Q(L1_4), .clr(reset));
  Register register_5 (.D(bit_in), .en(E5), .clk(clk), .Q(L1_5), .clr(reset));
  Register register_6 (.D(bit_in), .en(E6), .clk(clk), .Q(L1_6), .clr(reset));
  Register register_7 (.D(bit_in), .en(E7), .clk(clk), .Q(L1_7), .clr(reset));
  Register register_8 (.D(bit_in), .en(E1), .clk(clk), .Q(L2_1), .clr(reset));
  Register register_9 (.D(bit_in), .en(E2), .clk(clk), .Q(L2_2), .clr(reset));
  Register register_10 (.D(bit_in), .en(E3), .clk(clk), .Q(L2_3), .clr(reset));
  Register register_11 (.D(bit_in), .en(E4), .clk(clk), .Q(L2_4), .clr(reset));
  Register register_12 (.D(bit_in), .en(E5), .clk(clk), .Q(L2_5), .clr(reset));
  Register register_13 (.D(bit_in), .en(E6), .clk(clk), .Q(L2_6), .clr(reset));
  Register register_14 (.D(bit_in), .en(E7), .clk(clk), .Q(L2_7), .clr(reset));
  Decoder #(.select(3)) decoder_1 (
    .out1(E1), .out2(E2), .out3(E3), .out4(E4), .out5(E5), .out6(E6), .out7(E7), .sel(WRITE[2:0]));  // open: out0, en
  Multiplexer #(.select(3), .width(8)) multiplexer_1 (
    .in1(L1_1), .in2(L1_2), .in3(L1_3), .in4(L1_4), .in5(L1_5), .in6(L1_6), .in7(L1_7), .out(LEC1),
    .sel(READ1[2:0]));  // open: in0
  Multiplexer #(.select(3), .width(8)) multiplexer_2 (
    .in1(L2_1), .in2(L2_2), .in3(L2_3), .in4(L2_4), .in5(L2_5), .in6(L2_6), .in7(L2_7), .out(LEC2),
    .sel(READ2[2:0]));  // open: in0
endmodule

module clock_maison (
  input  clk,
  input  reset,
  input  run,
  input  halt_0,
  input  jumpif_0,
  input  jump_0,
  input  [7:0] bit_in,
  output [4:0] value_clk
);

  wire and_1_out, and_2_out, and_3_out, and_4_out, and_5_out, and_6_out, and_7_out, and_8_out, and_9_out,
       and_10_out, and_11_out, CLK_t, jump, multiplexer_1_out, multiplexer_2_out, multiplexer_3_out,
       multiplexer_4_out, multiplexer_5_out, or_6_out, R1, R2, R3, R4, R5, S0, S1, S2, S3, S4, start,
       xor_1_out, xor_2_out, xor_3_out, xor_4_out, xor_5_out;

  xor xor_1 (xor_1_out, 1'b1, value_clk[0]);
  xor xor_2 (xor_2_out, 1'b0, value_clk[1]);
  xor xor_3 (xor_3_out, 1'b0, value_clk[2]);
  xor xor_4 (xor_4_out, 1'b0, value_clk[3]);
  xor xor_5 (xor_5_out, 1'b0, value_clk[4]);
  xor xor_6 (S0, xor_1_out, 1'b0);
  and and_1 (and_1_out, 1'b0, xor_1_out);
  and and_2 (and_2_out, 1'b1, value_clk[0]);
  xor xor_7 (S1, xor_2_out, R1);
  and and_3 (and_3_out, R1, xor_2_out);
  and and_4 (and_4_out, 1'b0, value_clk[1]);
  xor xor_8 (S2, xor_3_out, R2);
  and and_5 (and_5_out, R2, xor_3_out);
  and and_6 (and_6_out, 1'b0, value_clk[2]);
  xor xor_9 (S3, xor_4_out, R3);
  and and_7 (and_7_out, R3, xor_4_out);
  and and_8 (and_8_out, 1'b0, value_clk[3]);
  xor xor_10 (S4, xor_5_out, R4);
  and and_9 (and_9_out, R4, xor_5_out);
  and and_10 (and_10_out, 1'b0, value_clk[4]);
  or or_1 (R1, and_1_out, and_2_out);
  or or_2 (R2, and_3_out, and_4_out);
  or or_3 (R3, and_5_out, and_6_out);
  or or_4 (R4, and_7_out, and_8_out);
  or or_5 (R5, and_9_out, and_10_out);
  Multiplexer multiplexer_1 (.in0(S0), .in1(bit_in[0]), .out(multiplexer_1_out), .sel(jump));
  D_Flip_Flop d_ff_1 (.D(multiplexer_1_out), .clk(CLK_t), .Q(value_clk[0]), .reset(reset));  // open: Qn, preset
  Multiplexer multiplexer_2 (.in0(S1), .in1(bit_in[1]), .out(multiplexer_2_out), .sel(jump));
  D_Flip_Flop d_ff_2 (.D(multiplexer_2_out), .clk(CLK_t), .Q(value_clk[1]), .reset(reset));  // open: Qn, preset
  Multiplexer multiplexer_3 (.in0(S2), .in1(bit_in[2]), .out(multiplexer_3_out), .sel(jump));
  D_Flip_Flop d_ff_3 (.D(multiplexer_3_out), .clk(CLK_t), .Q(value_clk[2]), .reset(reset));  // open: Qn, preset
  Multiplexer multiplexer_4 (.in0(S3), .in1(bit_in[3]), .out(multiplexer_4_out), .sel(jump));
  D_Flip_Flop d_ff_4 (.D(multiplexer_4_out), .clk(CLK_t), .Q(value_clk[3]), .reset(reset));  // open: Qn, preset
  Multiplexer multiplexer_5 (.in0(S4), .in1(bit_in[4]), .out(multiplexer_5_out), .sel(jump));
  D_Flip_Flop d_ff_5 (.D(multiplexer_5_out), .clk(CLK_t), .Q(value_clk[4]), .reset(reset));  // open: Qn, preset
  D_Flip_Flop d_ff_6 (.D(run), .clk(run), .Q(start), .reset(or_6_out));  // open: Qn, preset
  or or_6 (or_6_out, halt_0, and_11_out, reset);
  and and_11 (and_11_out, R5, value_clk[4], value_clk[3], value_clk[2], value_clk[1], value_clk[0]);
  and and_12 (CLK_t, clk, start);
  or or_7 (jump, jumpif_0, jump_0);

  // Other names for the same wires on the sheet: J0 = bit_in[0]; J1 = bit_in[1]; J2 = bit_in[2]; J3 = bit_in[3];
  //   J4 = bit_in[4]; J5 = bit_in[5]; J6 = bit_in[6]; J7 = bit_in[7]; halt = halt_0; A0 = value_clk[0];
  //   A1 = value_clk[1]; A2 = value_clk[2]; A3 = value_clk[3]; A4 = value_clk[4]
endmodule

module registre_code (
  input  load,
  input  reset,
  input  [4:0] value_clk,
  output [15:0] output_code
);

  wire [15:0] S0, S1, S2, S3, S4, S5, S6, S7, S8, S9, S10, S11, S12, S13, S14, S15, S16, S17, S18, S19, S20,
       S21, S22, S23, S24, S25, S26, S27, S28, S29, S30, S31, undriven, undriven_2, undriven_3, undriven_4,
       undriven_5, undriven_6, undriven_7, undriven_8, undriven_9, undriven_10, undriven_11, undriven_12,
       undriven_13, undriven_14, undriven_15, undriven_16, undriven_17, undriven_18, undriven_19,
       undriven_20, undriven_21, undriven_22, undriven_23, undriven_24, undriven_25, undriven_26,
       undriven_27, undriven_28, undriven_29, undriven_30, undriven_31, undriven_32;

  // DipSwitch #(.number(16)) dipswitch_1: pin names not known
  Register #(.width(16)) register_1 (.D(undriven), .en(load), .clk(load), .Q(S0), .clr(reset));
  // DipSwitch #(.number(16)) dipswitch_2: pin names not known
  Register #(.width(16)) register_2 (.D(undriven_2), .en(load), .clk(load), .Q(S8), .clr(reset));
  // DipSwitch #(.number(16)) dipswitch_3: pin names not known
  Register #(.width(16)) register_3 (.D(undriven_3), .en(load), .clk(load), .Q(S16), .clr(reset));
  // DipSwitch #(.number(16)) dipswitch_4: pin names not known
  Register #(.width(16)) register_4 (.D(undriven_4), .en(load), .clk(load), .Q(S24), .clr(reset));
  // DipSwitch #(.number(16)) dipswitch_5: pin names not known
  Register #(.width(16)) register_5 (.D(undriven_5), .en(load), .clk(load), .Q(S1), .clr(reset));
  // DipSwitch #(.number(16)) dipswitch_6: pin names not known
  Register #(.width(16)) register_6 (.D(undriven_6), .en(load), .clk(load), .Q(S9), .clr(reset));
  // DipSwitch #(.number(16)) dipswitch_7: pin names not known
  Register #(.width(16)) register_7 (.D(undriven_7), .en(load), .clk(load), .Q(S17), .clr(reset));
  // DipSwitch #(.number(16)) dipswitch_8: pin names not known
  Register #(.width(16)) register_8 (.D(undriven_8), .en(load), .clk(load), .Q(S25), .clr(reset));
  // DipSwitch #(.number(16)) dipswitch_9: pin names not known
  Register #(.width(16)) register_9 (.D(undriven_9), .en(load), .clk(load), .Q(S2), .clr(reset));
  // DipSwitch #(.number(16)) dipswitch_10: pin names not known
  Register #(.width(16)) register_10 (.D(undriven_10), .en(load), .clk(load), .Q(S10), .clr(reset));
  // DipSwitch #(.number(16)) dipswitch_11: pin names not known
  Register #(.width(16)) register_11 (.D(undriven_11), .en(load), .clk(load), .Q(S18), .clr(reset));
  // DipSwitch #(.number(16)) dipswitch_12: pin names not known
  Register #(.width(16)) register_12 (.D(undriven_12), .en(load), .clk(load), .Q(S26), .clr(reset));
  // DipSwitch #(.number(16)) dipswitch_13: pin names not known
  Register #(.width(16)) register_13 (.D(undriven_13), .en(load), .clk(load), .Q(S3), .clr(reset));
  // DipSwitch #(.number(16)) dipswitch_14: pin names not known
  Register #(.width(16)) register_14 (.D(undriven_14), .en(load), .clk(load), .Q(S11), .clr(reset));
  // DipSwitch #(.number(16)) dipswitch_15: pin names not known
  Register #(.width(16)) register_15 (.D(undriven_15), .en(load), .clk(load), .Q(S19), .clr(reset));
  // DipSwitch #(.number(16)) dipswitch_16: pin names not known
  Register #(.width(16)) register_16 (.D(undriven_16), .en(load), .clk(load), .Q(S27), .clr(reset));
  Multiplexer #(.select(5), .width(16)) multiplexer_1 (
    .in0(S0), .in1(S1), .in2(S2), .in3(S3), .in4(S4), .in5(S5), .in6(S6), .in7(S7), .in8(S8), .in9(S9),
    .in10(S10), .in11(S11), .in12(S12), .in13(S13), .in14(S14), .in15(S15), .in16(S16), .in17(S17),
    .in18(S18), .in19(S19), .in20(S20), .in21(S21), .in22(S22), .in23(S23), .in24(S24), .in25(S25),
    .in26(S26), .in27(S27), .in28(S28), .in29(S29), .in30(S30), .in31(S31), .out(output_code), .sel(value_clk));
  // DipSwitch #(.number(16)) dipswitch_17: pin names not known
  Register #(.width(16)) register_17 (.D(undriven_17), .en(load), .clk(load), .Q(S4), .clr(reset));
  // DipSwitch #(.number(16)) dipswitch_18: pin names not known
  Register #(.width(16)) register_18 (.D(undriven_18), .en(load), .clk(load), .Q(S12), .clr(reset));
  // DipSwitch #(.number(16)) dipswitch_19: pin names not known
  Register #(.width(16)) register_19 (.D(undriven_19), .en(load), .clk(load), .Q(S20), .clr(reset));
  // DipSwitch #(.number(16)) dipswitch_20: pin names not known
  Register #(.width(16)) register_20 (.D(undriven_20), .en(load), .clk(load), .Q(S28), .clr(reset));
  // DipSwitch #(.number(16)) dipswitch_21: pin names not known
  Register #(.width(16)) register_21 (.D(undriven_21), .en(load), .clk(load), .Q(S5), .clr(reset));
  // DipSwitch #(.number(16)) dipswitch_22: pin names not known
  Register #(.width(16)) register_22 (.D(undriven_22), .en(load), .clk(load), .Q(S13), .clr(reset));
  // DipSwitch #(.number(16)) dipswitch_23: pin names not known
  Register #(.width(16)) register_23 (.D(undriven_23), .en(load), .clk(load), .Q(S21), .clr(reset));
  // DipSwitch #(.number(16)) dipswitch_24: pin names not known
  Register #(.width(16)) register_24 (.D(undriven_24), .en(load), .clk(load), .Q(S29), .clr(reset));
  // DipSwitch #(.number(16)) dipswitch_25: pin names not known
  Register #(.width(16)) register_25 (.D(undriven_25), .en(load), .clk(load), .Q(S6), .clr(reset));
  // DipSwitch #(.number(16)) dipswitch_26: pin names not known
  Register #(.width(16)) register_26 (.D(undriven_26), .en(load), .clk(load), .Q(S14), .clr(reset));
  // DipSwitch #(.number(16)) dipswitch_27: pin names not known
  Register #(.width(16)) register_27 (.D(undriven_27), .en(load), .clk(load), .Q(S22), .clr(reset));
  // DipSwitch #(.number(16)) dipswitch_28: pin names not known
  Register #(.width(16)) register_28 (.D(undriven_28), .en(load), .clk(load), .Q(S30), .clr(reset));
  // DipSwitch #(.number(16)) dipswitch_29: pin names not known
  // DipSwitch #(.number(16)) dipswitch_30: pin names not known
  // DipSwitch #(.number(16)) dipswitch_31: pin names not known
  // DipSwitch #(.number(16)) dipswitch_32: pin names not known
  Register #(.width(16)) register_29 (.D(undriven_29), .en(load), .clk(load), .Q(S7), .clr(reset));
  Register #(.width(16)) register_30 (.D(undriven_30), .en(load), .clk(load), .Q(S15), .clr(reset));
  Register #(.width(16)) register_31 (.D(undriven_31), .en(load), .clk(load), .Q(S23), .clr(reset));
  Register #(.width(16)) register_32 (.D(undriven_32), .en(load), .clk(load), .Q(S31), .clr(reset));
endmodule
