// Logisim project CPU.circ as structural Verilog: 5 circuits, main circuit main
module main (
);

  wire ADD_0, AND_0, and_1_out, clk, d_ff_1_q, HALT_0, JUMP_0, JUMPIF_0, JUMPIF_1, load, LOAD_0,
       n7_segment_display_1_p1, n7_segment_display_2_p1, n7_segment_display_3_p1, NAND_0, NOR_0, not_1_out,
       not_2_out, not_3_out, not_4_out, not_5_out, not_6_out, not_7_out, not_8_out, OR_0, R, R1, R2, R3, R4,
       R5, R6, R7, R8, R9, R10, R11, R12, R13, R14, R15, rst, run, SUB_0, XNOR_0, XOR_0;
  wire [3:0] multiplexer_1_out, opp, read, read1, read2, write;
  wire [5:0] clock_maison_1_value_clk;
  wire [7:0] LEC1, LEC2, multiplexer_2_out, multiplexer_3_out, OUTPUT_ALU;

  ALU_maison alu_maison_1 (.opp(opp), .INPUT_A(LEC1), .INPUT_B(LEC2), .OUTPUT_ALU(OUTPUT_ALU));
  Multiplexer #(.width(4)) multiplexer_1 (.in0(read1), .in1(read), .out(multiplexer_1_out), .sel(R));
  Multiplexer #(.width(8)) multiplexer_2 (
    .in0(OUTPUT_ALU), .in1({read2, read1}), .out(multiplexer_2_out), .sel(LOAD_0));
  Multiplexer #(.select(2), .width(8)) multiplexer_3 (
    .in0(OUTPUT_ALU), .in1({read2, read1}), .in2({read2, read1}), .out(multiplexer_3_out),
    .sel({JUMPIF_1, JUMP_0}));  // open: in3
  registre_cpu registre_cpu_1 (
    .W(write), .R1(multiplexer_1_out), .R2(read2), .clk(clk), .reset(rst), .Data(multiplexer_2_out),
    .L1(LEC1), .L2(LEC2));
  not not_1 (not_1_out, OUTPUT_ALU[1]);
  not not_2 (not_2_out, OUTPUT_ALU[3]);
  not not_3 (not_3_out, OUTPUT_ALU[5]);
  not not_4 (not_4_out, OUTPUT_ALU[7]);
  clock_maison clock_maison_1 (
    .run(run), .halt_0(HALT_0), .jumpif_0(JUMPIF_1), .jump_0(JUMP_0), .clk(clk), .reset(rst),
    .bit_in(multiplexer_3_out), .value_clk(clock_maison_1_value_clk));
  not not_5 (not_5_out, OUTPUT_ALU[0]);
  not not_6 (not_6_out, OUTPUT_ALU[2]);
  not not_7 (not_7_out, OUTPUT_ALU[4]);
  not not_8 (not_8_out, OUTPUT_ALU[6]);
  and and_1 (and_1_out, not_5_out, not_1_out, not_6_out, not_2_out, not_7_out, not_3_out, not_8_out, not_4_out);
  D_Flip_Flop d_ff_1 (.D(and_1_out), .clk(clk), .Q(d_ff_1_q), .reset(rst));  // open: Qn, preset
  and and_2 (JUMPIF_1, JUMPIF_0, d_ff_1_q);
  registre_code registre_code_1 (
    .reset(rst), .load(load), .value_clk(clock_maison_1_value_clk), .output_code({read1, read2, write, opp}));
  Decoder #(.select(4)) decoder_1 (
    .out0(ADD_0), .out1(OR_0), .out2(XNOR_0), .out3(NAND_0), .out4(NOR_0), .out5(XOR_0), .out6(AND_0),
    .out7(SUB_0), .out8(LOAD_0), .out9(HALT_0), .out10(JUMP_0), .out11(JUMPIF_0), .sel(opp));  // open: out12, out13, out14, out15, en
  Button reset (.out(rst));
  Button load_code (.out(load));
  Button run_clock (.out(run));
  Clock clock_1 (.out(clk));
  // BCD_to_7_Segment_decoder bcd_to_7_segment_decoder_1: pin names not known
  // _7_Segment_Display 7_segment_display_1: pin names not known; wires that end beside it: n7_segment_display_1_p1, n7_segment_display_1_p1
  // Binary_to_BCD_converter #(.binvalue(8)) binary_to_bcd_converter_1: pin names not known; wires that end beside it: LEC1
  LED led_1 (.in(clk));
  // BCD_to_7_Segment_decoder bcd_to_7_segment_decoder_2: pin names not known
  // BCD_to_7_Segment_decoder bcd_to_7_segment_decoder_3: pin names not known
  // _7_Segment_Display 7_segment_display_2: pin names not known; wires that end beside it: n7_segment_display_2_p1, n7_segment_display_2_p1
  // _7_Segment_Display 7_segment_display_3: pin names not known; wires that end beside it: n7_segment_display_3_p1, n7_segment_display_3_p1
  // DipSwitch #(.number(1)) READ_R1: pin names not known; wires that end beside it: R1
  // DipSwitch #(.number(1)) READ_R2: pin names not known; wires that end beside it: R2
  // DipSwitch #(.number(1)) READ_R3: pin names not known; wires that end beside it: R3
  // DipSwitch #(.number(1)) READ_R4: pin names not known; wires that end beside it: R4
  // DipSwitch #(.number(1)) READ_R5: pin names not known; wires that end beside it: R5
  // DipSwitch #(.number(1)) READ_R6: pin names not known; wires that end beside it: R6
  // DipSwitch #(.number(1)) READ_R7: pin names not known; wires that end beside it: R7
  // DipSwitch #(.number(1)) READ_R8: pin names not known; wires that end beside it: R8
  // DipSwitch #(.number(1)) READ_R9: pin names not known; wires that end beside it: R9
  // DipSwitch #(.number(1)) READ_R10: pin names not known; wires that end beside it: R10
  // DipSwitch #(.number(1)) READ_R11: pin names not known; wires that end beside it: R11
  // DipSwitch #(.number(1)) READ_R12: pin names not known; wires that end beside it: R12
  // DipSwitch #(.number(1)) READ_R13: pin names not known; wires that end beside it: R13
  // DipSwitch #(.number(1)) READ_R14: pin names not known; wires that end beside it: R14
  // DipSwitch #(.number(1)) READ_R15: pin names not known; wires that end beside it: R15
  assign read = R1 ? 4'b0001 : 4'bz;  // Controlled_Buffer controlled_buffer_1
  assign read = R5 ? 4'b0101 : 4'bz;  // Controlled_Buffer controlled_buffer_2
  assign read = R9 ? 4'b1001 : 4'bz;  // Controlled_Buffer controlled_buffer_3
  assign read = R13 ? 4'b1101 : 4'bz;  // Controlled_Buffer controlled_buffer_4
  assign read = R2 ? 4'b0010 : 4'bz;  // Controlled_Buffer controlled_buffer_5
  assign read = R6 ? 4'b0110 : 4'bz;  // Controlled_Buffer controlled_buffer_6
  assign read = R10 ? 4'b1010 : 4'bz;  // Controlled_Buffer controlled_buffer_7
  assign read = R14 ? 4'b1110 : 4'bz;  // Controlled_Buffer controlled_buffer_8
  assign read = R3 ? 4'b0011 : 4'bz;  // Controlled_Buffer controlled_buffer_9
  assign read = R7 ? 4'b0111 : 4'bz;  // Controlled_Buffer controlled_buffer_10
  assign read = R11 ? 4'b1011 : 4'bz;  // Controlled_Buffer controlled_buffer_11
  assign read = R15 ? 4'b1111 : 4'bz;  // Controlled_Buffer controlled_buffer_12
  assign read = R4 ? 4'b0100 : 4'bz;  // Controlled_Buffer controlled_buffer_13
  assign read = R8 ? 4'b1000 : 4'bz;  // Controlled_Buffer controlled_buffer_14
  assign read = R12 ? 4'b1100 : 4'bz;  // Controlled_Buffer controlled_buffer_15
  or or_1 (R, R1, R2, R3, R4, R5, R6, R7, R8, R9, R10, R11, R12, R13, R14, R15);

  // Notes on the sheet:
  //   FLAG ALU
endmodule

module ALU_maison (
  input  [3:0] opp,
  input  [7:0] INPUT_A,
  input  [7:0] INPUT_B,
  output [7:0] OUTPUT_ALU
);

  wire and_1_out, and_2_out, and_3_out, and_4_out, and_5_out, and_6_out, and_7_out, and_8_out, and_9_out,
       and_10_out, and_11_out, and_12_out, and_13_out, and_14_out, and_15_out, and_16_out, and_17_out,
       and_18_out, and_19_out, and_20_out, and_21_out, and_22_out, and_23_out, and_24_out, and_25_out,
       and_26_out, and_27_out, and_28_out, and_29_out, and_30_out, and_31_out, and_32_out, not_1_out,
       not_2_out, not_3_out, not_4_out, not_5_out, not_6_out, not_7_out, not_8_out, or_8_out, or_16_out, R0,
       R0b, R1, R1b, R2, R2b, R3, R3b, R4, R4b, R5, R5b, R6, R6b, xor_1_out, xor_2_out, xor_3_out, xor_4_out,
       xor_5_out, xor_6_out, xor_7_out, xor_8_out, xor_17_out, xor_18_out, xor_19_out, xor_20_out,
       xor_21_out, xor_22_out, xor_23_out, xor_24_out;
  wire [7:0] S_ADD, S_AND, S_NAND, S_NOR, S_NXOR, S_OR, S_SUB, S_XOR;

  Multiplexer #(.select(4), .width(8)) multiplexer_1 (
    .in0(S_ADD), .in1(S_OR), .in2(S_NXOR), .in3(S_NAND), .in4(S_NOR), .in5(S_XOR), .in6(S_AND), .in7(S_SUB),
    .out(OUTPUT_ALU), .sel(opp));  // open: in8, in9, in10, in11, in12, in13, in14, in15
  xor xor_1 (xor_1_out, INPUT_A[0], INPUT_B[0]);
  xor xor_2 (xor_2_out, INPUT_A[1], INPUT_B[1]);
  xor xor_3 (xor_3_out, INPUT_A[2], INPUT_B[2]);
  xor xor_4 (xor_4_out, INPUT_A[3], INPUT_B[3]);
  xor xor_5 (xor_5_out, INPUT_A[4], INPUT_B[4]);
  xor xor_6 (xor_6_out, INPUT_A[5], INPUT_B[5]);
  xor xor_7 (xor_7_out, INPUT_A[6], INPUT_B[6]);
  xor xor_8 (xor_8_out, INPUT_A[7], INPUT_B[7]);
  and and_1 (and_1_out, 1'b0, xor_1_out);
  and and_2 (and_2_out, INPUT_B[0], INPUT_A[0]);
  and and_3 (and_3_out, R0, xor_2_out);
  and and_4 (and_4_out, INPUT_B[1], INPUT_A[1]);
  and and_5 (and_5_out, R1, xor_3_out);
  and and_6 (and_6_out, INPUT_B[2], INPUT_A[2]);
  and and_7 (and_7_out, R2, xor_4_out);
  and and_8 (and_8_out, INPUT_B[3], INPUT_A[3]);
  and and_9 (and_9_out, R3, xor_5_out);
  and and_10 (and_10_out, INPUT_B[4], INPUT_A[4]);
  and and_11 (and_11_out, R4, xor_6_out);
  and and_12 (and_12_out, INPUT_B[5], INPUT_A[5]);
  and and_13 (and_13_out, R5, xor_7_out);
  and and_14 (and_14_out, INPUT_B[6], INPUT_A[6]);
  and and_15 (and_15_out, R6, xor_8_out);
  and and_16 (and_16_out, INPUT_B[7], INPUT_A[7]);
  xor xor_9 (S_ADD[0], xor_1_out, 1'b0);
  or or_1 (R0, and_1_out, and_2_out);
  xor xor_10 (S_ADD[1], xor_2_out, R0);
  or or_2 (R1, and_3_out, and_4_out);
  xor xor_11 (S_ADD[2], xor_3_out, R1);
  or or_3 (R2, and_5_out, and_6_out);
  xor xor_12 (S_ADD[3], xor_4_out, R2);
  or or_4 (R3, and_7_out, and_8_out);
  xor xor_13 (S_ADD[4], xor_5_out, R3);
  or or_5 (R4, and_9_out, and_10_out);
  xor xor_14 (S_ADD[5], xor_6_out, R4);
  or or_6 (R5, and_11_out, and_12_out);
  xor xor_15 (S_ADD[6], xor_7_out, R5);
  or or_7 (R6, and_13_out, and_14_out);
  xor xor_16 (S_ADD[7], xor_8_out, R6);
  or or_8 (or_8_out, and_15_out, and_16_out);
  LED led_1 (.in(or_8_out));
  not not_1 (not_1_out, INPUT_B[0]);
  not not_2 (not_2_out, INPUT_B[1]);
  not not_3 (not_3_out, INPUT_B[2]);
  not not_4 (not_4_out, INPUT_B[3]);
  not not_5 (not_5_out, INPUT_B[4]);
  not not_6 (not_6_out, INPUT_B[5]);
  not not_7 (not_7_out, INPUT_B[6]);
  not not_8 (not_8_out, INPUT_B[7]);
  xor xor_17 (xor_17_out, INPUT_A[0], not_1_out);
  xor xor_18 (xor_18_out, INPUT_A[1], not_2_out);
  xor xor_19 (xor_19_out, INPUT_A[2], not_3_out);
  xor xor_20 (xor_20_out, INPUT_A[3], not_4_out);
  xor xor_21 (xor_21_out, INPUT_A[4], not_5_out);
  xor xor_22 (xor_22_out, INPUT_A[5], not_6_out);
  xor xor_23 (xor_23_out, INPUT_A[6], not_7_out);
  xor xor_24 (xor_24_out, INPUT_A[7], not_8_out);
  xor xor_25 (S_SUB[0], xor_17_out, 1'b1);
  and and_17 (and_17_out, 1'b1, xor_17_out);
  and and_18 (and_18_out, not_1_out, INPUT_A[0]);
  xor xor_26 (S_SUB[1], xor_18_out, R0b);
  and and_19 (and_19_out, R0b, xor_18_out);
  and and_20 (and_20_out, not_2_out, INPUT_A[1]);
  xor xor_27 (S_SUB[2], xor_19_out, R1b);
  and and_21 (and_21_out, R1b, xor_19_out);
  and and_22 (and_22_out, not_3_out, INPUT_A[2]);
  xor xor_28 (S_SUB[3], xor_20_out, R2b);
  and and_23 (and_23_out, R2b, xor_20_out);
  and and_24 (and_24_out, not_4_out, INPUT_A[3]);
  xor xor_29 (S_SUB[4], xor_21_out, R3b);
  and and_25 (and_25_out, R3b, xor_21_out);
  and and_26 (and_26_out, not_5_out, INPUT_A[4]);
  xor xor_30 (S_SUB[5], xor_22_out, R4b);
  and and_27 (and_27_out, R4b, xor_22_out);
  and and_28 (and_28_out, not_6_out, INPUT_A[5]);
  xor xor_31 (S_SUB[6], xor_23_out, R5b);
  and and_29 (and_29_out, R5b, xor_23_out);
  and and_30 (and_30_out, not_7_out, INPUT_A[6]);
  xor xor_32 (S_SUB[7], xor_24_out, R6b);
  and and_31 (and_31_out, R6b, xor_24_out);
  and and_32 (and_32_out, not_8_out, INPUT_A[7]);
  or or_9 (R0b, and_17_out, and_18_out);
  or or_10 (R1b, and_19_out, and_20_out);
  or or_11 (R2b, and_21_out, and_22_out);
  or or_12 (R3b, and_23_out, and_24_out);
  or or_13 (R4b, and_25_out, and_26_out);
  or or_14 (R5b, and_27_out, and_28_out);
  or or_15 (R6b, and_29_out, and_30_out);
  or or_16 (or_16_out, and_31_out, and_32_out);
  LED led_2 (.in(or_16_out));
  assign S_AND = INPUT_A & INPUT_B;  // AND_Gate and_33, 8 bits wide
  assign S_OR = INPUT_A | INPUT_B;  // OR_Gate or_17, 8 bits wide
  assign S_NAND = ~(INPUT_A & INPUT_B);  // NAND_Gate nand_1, 8 bits wide
  assign S_NOR = ~(INPUT_A | INPUT_B);  // NOR_Gate nor_1, 8 bits wide
  assign S_XOR = INPUT_A ^ INPUT_B;  // XOR_Gate xor_33, 8 bits wide
  assign S_NXOR = ~(INPUT_A ^ INPUT_B);  // XNOR_Gate xnor_1, 8 bits wide

  // Other names for the same wires on the sheet: N1[7:0] = INPUT_A; N1_0 = INPUT_A[0]; N1_1 = INPUT_A[1];
  //   N1_2 = INPUT_A[2]; N1_3 = INPUT_A[3]; N1_4 = INPUT_A[4]; N1_5 = INPUT_A[5]; N1_6 = INPUT_A[6];
  //   N1_7 = INPUT_A[7]; N2[7:0] = INPUT_B; N2_0 = INPUT_B[0]; N2_1 = INPUT_B[1]; N2_2 = INPUT_B[2];
  //   N2_3 = INPUT_B[3]; N2_4 = INPUT_B[4]; N2_5 = INPUT_B[5]; N2_6 = INPUT_B[6]; N2_7 = INPUT_B[7]
endmodule

module registre_cpu (
  input  [3:0] W,
  input  [3:0] R1,
  input  [3:0] R2,
  input  [7:0] Data,
  input  clk,
  input  reset,
  output [7:0] L1,
  output [7:0] L2
);

  wire E1, E2, E3, E4, E5, E6, E7, E8, E9, E10, E11, E12, E13, E14, E15;
  wire [7:0] L1_1, L1_2, L1_3, L1_4, L1_5, L1_6, L1_7, L1_8, L1_9, L1_10, L1_11, L1_12, L1_13, L1_14, L1_15,
       L2_1, L2_2, L2_3, L2_4, L2_5, L2_6, L2_7, L2_8, L2_9, L2_10, L2_11, L2_12, L2_13, L2_14, L2_15;

  Register register_1 (.D(Data), .en(E1), .clk(clk), .Q(L1_1), .clr(reset));
  Register register_2 (.D(Data), .en(E2), .clk(clk), .Q(L1_2), .clr(reset));
  Register register_3 (.D(Data), .en(E3), .clk(clk), .Q(L1_3), .clr(reset));
  Register register_4 (.D(Data), .en(E4), .clk(clk), .Q(L1_4), .clr(reset));
  Register register_5 (.D(Data), .en(E5), .clk(clk), .Q(L1_5), .clr(reset));
  Register register_6 (.D(Data), .en(E6), .clk(clk), .Q(L1_6), .clr(reset));
  Register register_7 (.D(Data), .en(E7), .clk(clk), .Q(L1_7), .clr(reset));
  Register register_8 (.D(Data), .en(E8), .clk(clk), .Q(L1_8), .clr(reset));
  Register register_9 (.D(Data), .en(E9), .clk(clk), .Q(L1_9), .clr(reset));
  Register register_10 (.D(Data), .en(E10), .clk(clk), .Q(L1_10), .clr(reset));
  Register register_11 (.D(Data), .en(E11), .clk(clk), .Q(L1_11), .clr(reset));
  Register register_12 (.D(Data), .en(E12), .clk(clk), .Q(L1_12), .clr(reset));
  Register register_13 (.D(Data), .en(E13), .clk(clk), .Q(L1_13), .clr(reset));
  Register register_14 (.D(Data), .en(E14), .clk(clk), .Q(L1_14), .clr(reset));
  Register register_15 (.D(Data), .en(E15), .clk(clk), .Q(L1_15), .clr(reset));
  Register register_16 (.D(Data), .en(E1), .clk(clk), .Q(L2_1), .clr(reset));
  Register register_17 (.D(Data), .en(E2), .clk(clk), .Q(L2_2), .clr(reset));
  Register register_18 (.D(Data), .en(E3), .clk(clk), .Q(L2_3), .clr(reset));
  Register register_19 (.D(Data), .en(E4), .clk(clk), .Q(L2_4), .clr(reset));
  Register register_20 (.D(Data), .en(E5), .clk(clk), .Q(L2_5), .clr(reset));
  Register register_21 (.D(Data), .en(E6), .clk(clk), .Q(L2_6), .clr(reset));
  Register register_22 (.D(Data), .en(E7), .clk(clk), .Q(L2_7), .clr(reset));
  Register register_23 (.D(Data), .en(E8), .clk(clk), .Q(L2_8), .clr(reset));
  Register register_24 (.D(Data), .en(E9), .clk(clk), .Q(L2_9), .clr(reset));
  Register register_25 (.D(Data), .en(E10), .clk(clk), .Q(L2_10), .clr(reset));
  Register register_26 (.D(Data), .en(E11), .clk(clk), .Q(L2_11), .clr(reset));
  Register register_27 (.D(Data), .en(E12), .clk(clk), .Q(L2_12), .clr(reset));
  Register register_28 (.D(Data), .en(E13), .clk(clk), .Q(L2_13), .clr(reset));
  Register register_29 (.D(Data), .en(E14), .clk(clk), .Q(L2_14), .clr(reset));
  Register register_30 (.D(Data), .en(E15), .clk(clk), .Q(L2_15), .clr(reset));
  Decoder #(.select(4)) decoder_1 (
    .out1(E1), .out2(E2), .out3(E3), .out4(E4), .out5(E5), .out6(E6), .out7(E7), .out8(E8), .out9(E9),
    .out10(E10), .out11(E11), .out12(E12), .out13(E13), .out14(E14), .out15(E15), .sel(W));  // open: out0, en
  Multiplexer #(.select(4), .width(8)) multiplexer_1 (
    .in1(L1_1), .in2(L1_2), .in3(L1_3), .in4(L1_4), .in5(L1_5), .in6(L1_6), .in7(L1_7), .in8(L1_8),
    .in9(L1_9), .in10(L1_10), .in11(L1_11), .in12(L1_12), .in13(L1_13), .in14(L1_14), .in15(L1_15), .out(L1),
    .sel(R1));  // open: in0
  Multiplexer #(.select(4), .width(8)) multiplexer_2 (
    .in1(L2_1), .in2(L2_2), .in3(L2_3), .in4(L2_4), .in5(L2_5), .in6(L2_6), .in7(L2_7), .in8(L2_8),
    .in9(L2_9), .in10(L2_10), .in11(L2_11), .in12(L2_12), .in13(L2_13), .in14(L2_14), .in15(L2_15), .out(L2),
    .sel(R2));  // open: in0

  // Other names for the same wires on the sheet: bit_in[7:0] = Data; LEC1[7:0] = L1; LEC2[7:0] = L2; READ1[3:0] = R1;
  //   READ2[3:0] = R2; WRITE[3:0] = W
endmodule

module clock_maison (
  input  clk,
  input  reset,
  input  run,
  input  halt_0,
  input  jumpif_0,
  input  jump_0,
  input  [7:0] bit_in,
  output [5:0] value_clk
);

  wire and_1_out, and_2_out, and_3_out, and_4_out, and_5_out, and_6_out, and_7_out, and_8_out, and_9_out,
       and_10_out, and_11_out, and_12_out, and_13_out, CLK_t, jump, multiplexer_1_out, multiplexer_2_out,
       multiplexer_3_out, multiplexer_4_out, multiplexer_5_out, multiplexer_6_out, or_7_out, R1, R2, R3, R4,
       R5, R6, S0, S1, S2, S3, S4, S5, start, xor_1_out, xor_2_out, xor_3_out, xor_4_out, xor_5_out,
       xor_6_out;

  xor xor_1 (xor_1_out, 1'b1, value_clk[0]);
  xor xor_2 (xor_2_out, 1'b0, value_clk[1]);
  xor xor_3 (xor_3_out, 1'b0, value_clk[2]);
  xor xor_4 (xor_4_out, 1'b0, value_clk[3]);
  xor xor_5 (xor_5_out, 1'b0, value_clk[4]);
  xor xor_6 (xor_6_out, 1'b0, value_clk[5]);
  xor xor_7 (S0, xor_1_out, 1'b0);
  and and_1 (and_1_out, 1'b0, xor_1_out);
  and and_2 (and_2_out, 1'b1, value_clk[0]);
  xor xor_8 (S1, xor_2_out, R1);
  and and_3 (and_3_out, R1, xor_2_out);
  and and_4 (and_4_out, 1'b0, value_clk[1]);
  xor xor_9 (S2, xor_3_out, R2);
  and and_5 (and_5_out, R2, xor_3_out);
  and and_6 (and_6_out, 1'b0, value_clk[2]);
  xor xor_10 (S3, xor_4_out, R3);
  and and_7 (and_7_out, R3, xor_4_out);
  and and_8 (and_8_out, 1'b0, value_clk[3]);
  xor xor_11 (S4, xor_5_out, R4);
  and and_9 (and_9_out, R4, xor_5_out);
  and and_10 (and_10_out, 1'b0, value_clk[4]);
  xor xor_12 (S5, xor_6_out, R5);
  and and_11 (and_11_out, R5, xor_6_out);
  and and_12 (and_12_out, 1'b0, value_clk[5]);
  or or_1 (R1, and_1_out, and_2_out);
  or or_2 (R2, and_3_out, and_4_out);
  or or_3 (R3, and_5_out, and_6_out);
  or or_4 (R4, and_7_out, and_8_out);
  or or_5 (R5, and_9_out, and_10_out);
  or or_6 (R6, and_11_out, and_12_out);
  Multiplexer multiplexer_1 (.in0(S0), .in1(bit_in[0]), .out(multiplexer_1_out), .sel(jump));
  D_Flip_Flop d_ff_1 (.D(multiplexer_1_out), .clk(CLK_t), .Q(value_clk[0]), .reset(reset));  // open: Qn, preset
  Multiplexer multiplexer_2 (.in0(S1), .in1(bit_in[1]), .out(multiplexer_2_out), .sel(jump));
  D_Flip_Flop d_ff_2 (.D(multiplexer_2_out), .clk(CLK_t), .Q(value_clk[1]), .reset(reset));  // open: Qn, preset
  Multiplexer multiplexer_3 (.in0(S2), .in1(bit_in[2]), .out(multiplexer_3_out), .sel(jump));
  D_Flip_Flop d_ff_3 (.D(multiplexer_3_out), .clk(CLK_t), .Q(value_clk[2]), .reset(reset));  // open: Qn, preset
  Multiplexer multiplexer_4 (.in0(S3), .in1(bit_in[3]), .out(multiplexer_4_out), .sel(jump));
  D_Flip_Flop d_ff_4 (.D(multiplexer_4_out), .clk(CLK_t), .Q(value_clk[3]), .reset(reset));  // open: Qn, preset
  Multiplexer multiplexer_5 (.in0(S4), .in1(bit_in[4]), .out(multiplexer_5_out), .sel(jump));
  D_Flip_Flop d_ff_5 (.D(multiplexer_5_out), .clk(CLK_t), .Q(value_clk[4]), .reset(reset));  // open: Qn, preset
  Multiplexer multiplexer_6 (.in0(S5), .in1(bit_in[5]), .out(multiplexer_6_out), .sel(jump));
  D_Flip_Flop d_ff_6 (.D(multiplexer_6_out), .clk(CLK_t), .Q(value_clk[5]), .reset(reset));  // open: Qn, preset
  D_Flip_Flop d_ff_7 (.D(run), .clk(run), .Q(start), .reset(or_7_out));  // open: Qn, preset
  or or_7 (or_7_out, halt_0, and_13_out, reset);
  and and_13 (and_13_out, R5, value_clk[5], value_clk[4], value_clk[3], value_clk[2], value_clk[1], value_clk[0]);
  and and_14 (CLK_t, clk, start);
  or or_8 (jump, jumpif_0, jump_0);

  // Other names for the same wires on the sheet: J0 = bit_in[0]; J1 = bit_in[1]; J2 = bit_in[2]; J3 = bit_in[3];
  //   J4 = bit_in[4]; J5 = bit_in[5]; J6 = bit_in[6]; J7 = bit_in[7]; halt = halt_0; A0 = value_clk[0];
  //   A1 = value_clk[1]; A2 = value_clk[2]; A3 = value_clk[3]; A4 = value_clk[4]; A5 = value_clk[5]
endmodule

module registre_code (
  input  load,
  input  reset,
  input  [5:0] value_clk,
  output [15:0] output_code
);

  wire [15:0] S0, S1, S2, S3, S4, S5, S6, S7, S8, S9, S10, S11, S12, S13, S14, S15, S16, S17, S18, S19, S20,
       S21, S22, S23, S24, S25, S26, S27, S28, S29, S30, S31, S32, S33, S34, S35, S36, S37, S38, S39, S40,
       S41, S42, S43, S44, S45, S46, S47, S48, S49, S50, S51, S52, S53, S54, S55, S56, S57, S58, S59, S60,
       S61, S62, S63, undriven, undriven_2, undriven_3, undriven_4, undriven_5, undriven_6, undriven_7,
       undriven_8, undriven_9, undriven_10, undriven_11, undriven_12, undriven_13, undriven_14, undriven_15,
       undriven_16, undriven_17, undriven_18, undriven_19, undriven_20, undriven_21, undriven_22,
       undriven_23, undriven_24, undriven_25, undriven_26, undriven_27, undriven_28, undriven_29,
       undriven_30, undriven_31, undriven_32, undriven_33, undriven_34, undriven_35, undriven_36,
       undriven_37, undriven_38, undriven_39, undriven_40, undriven_41, undriven_42, undriven_43,
       undriven_44, undriven_45, undriven_46, undriven_47, undriven_48, undriven_49, undriven_50,
       undriven_51, undriven_52, undriven_53, undriven_54, undriven_55, undriven_56, undriven_57,
       undriven_58, undriven_59, undriven_60, undriven_61, undriven_62, undriven_63, undriven_64;

  // DipSwitch #(.number(16)) dipswitch_1: pin names not known
  Register #(.width(16)) register_1 (.D(undriven), .en(load), .clk(load), .Q(S0), .clr(reset));
  // DipSwitch #(.number(16)) dipswitch_2: pin names not known
  Register #(.width(16)) register_2 (.D(undriven_2), .en(load), .clk(load), .Q(S8), .clr(reset));
  // DipSwitch #(.number(16)) dipswitch_3: pin names not known
  Register #(.width(16)) register_3 (.D(undriven_3), .en(load), .clk(load), .Q(S16), .clr(reset));
  // DipSwitch #(.number(16)) dipswitch_4: pin names not known
  Register #(.width(16)) register_4 (.D(undriven_4), .en(load), .clk(load), .Q(S24), .clr(reset));
  // DipSwitch #(.number(16)) dipswitch_5: pin names not known
  Register #(.width(16)) register_5 (.D(undriven_5), .en(load), .clk(load), .Q(S32), .clr(reset));
  // DipSwitch #(.number(16)) dipswitch_6: pin names not known
  Register #(.width(16)) register_6 (.D(undriven_6), .en(load), .clk(load), .Q(S40), .clr(reset));
  // DipSwitch #(.number(16)) dipswitch_7: pin names not known
  Register #(.width(16)) register_7 (.D(undriven_7), .en(load), .clk(load), .Q(S48), .clr(reset));
  // DipSwitch #(.number(16)) dipswitch_8: pin names not known
  Register #(.width(16)) register_8 (.D(undriven_8), .en(load), .clk(load), .Q(S56), .clr(reset));
  // DipSwitch #(.number(16)) dipswitch_9: pin names not known
  Register #(.width(16)) register_9 (.D(undriven_9), .en(load), .clk(load), .Q(S1), .clr(reset));
  // DipSwitch #(.number(16)) dipswitch_10: pin names not known
  Register #(.width(16)) register_10 (.D(undriven_10), .en(load), .clk(load), .Q(S9), .clr(reset));
  // DipSwitch #(.number(16)) dipswitch_11: pin names not known
  Register #(.width(16)) register_11 (.D(undriven_11), .en(load), .clk(load), .Q(S17), .clr(reset));
  // DipSwitch #(.number(16)) dipswitch_12: pin names not known
  Register #(.width(16)) register_12 (.D(undriven_12), .en(load), .clk(load), .Q(S25), .clr(reset));
  // DipSwitch #(.number(16)) dipswitch_13: pin names not known
  Register #(.width(16)) register_13 (.D(undriven_13), .en(load), .clk(load), .Q(S33), .clr(reset));
  // DipSwitch #(.number(16)) dipswitch_14: pin names not known
  Register #(.width(16)) register_14 (.D(undriven_14), .en(load), .clk(load), .Q(S41), .clr(reset));
  // DipSwitch #(.number(16)) dipswitch_15: pin names not known
  Register #(.width(16)) register_15 (.D(undriven_15), .en(load), .clk(load), .Q(S49), .clr(reset));
  // DipSwitch #(.number(16)) dipswitch_16: pin names not known
  Register #(.width(16)) register_16 (.D(undriven_16), .en(load), .clk(load), .Q(S57), .clr(reset));
  // DipSwitch #(.number(16)) dipswitch_17: pin names not known
  Register #(.width(16)) register_17 (.D(undriven_17), .en(load), .clk(load), .Q(S2), .clr(reset));
  // DipSwitch #(.number(16)) dipswitch_18: pin names not known
  Register #(.width(16)) register_18 (.D(undriven_18), .en(load), .clk(load), .Q(S10), .clr(reset));
  // DipSwitch #(.number(16)) dipswitch_19: pin names not known
  Register #(.width(16)) register_19 (.D(undriven_19), .en(load), .clk(load), .Q(S18), .clr(reset));
  // DipSwitch #(.number(16)) dipswitch_20: pin names not known
  Register #(.width(16)) register_20 (.D(undriven_20), .en(load), .clk(load), .Q(S26), .clr(reset));
  // DipSwitch #(.number(16)) dipswitch_21: pin names not known
  Register #(.width(16)) register_21 (.D(undriven_21), .en(load), .clk(load), .Q(S34), .clr(reset));
  // DipSwitch #(.number(16)) dipswitch_22: pin names not known
  Register #(.width(16)) register_22 (.D(undriven_22), .en(load), .clk(load), .Q(S42), .clr(reset));
  // DipSwitch #(.number(16)) dipswitch_23: pin names not known
  Register #(.width(16)) register_23 (.D(undriven_23), .en(load), .clk(load), .Q(S50), .clr(reset));
  // DipSwitch #(.number(16)) dipswitch_24: pin names not known
  Register #(.width(16)) register_24 (.D(undriven_24), .en(load), .clk(load), .Q(S58), .clr(reset));
  // DipSwitch #(.number(16)) dipswitch_25: pin names not known
  Register #(.width(16)) register_25 (.D(undriven_25), .en(load), .clk(load), .Q(S3), .clr(reset));
  // DipSwitch #(.number(16)) dipswitch_26: pin names not known
  Register #(.width(16)) register_26 (.D(undriven_26), .en(load), .clk(load), .Q(S11), .clr(reset));
  // DipSwitch #(.number(16)) dipswitch_27: pin names not known
  Register #(.width(16)) register_27 (.D(undriven_27), .en(load), .clk(load), .Q(S19), .clr(reset));
  // DipSwitch #(.number(16)) dipswitch_28: pin names not known
  Register #(.width(16)) register_28 (.D(undriven_28), .en(load), .clk(load), .Q(S27), .clr(reset));
  // DipSwitch #(.number(16)) dipswitch_29: pin names not known
  Register #(.width(16)) register_29 (.D(undriven_29), .en(load), .clk(load), .Q(S35), .clr(reset));
  // DipSwitch #(.number(16)) dipswitch_30: pin names not known
  Register #(.width(16)) register_30 (.D(undriven_30), .en(load), .clk(load), .Q(S43), .clr(reset));
  // DipSwitch #(.number(16)) dipswitch_31: pin names not known
  Register #(.width(16)) register_31 (.D(undriven_31), .en(load), .clk(load), .Q(S51), .clr(reset));
  // DipSwitch #(.number(16)) dipswitch_32: pin names not known
  Register #(.width(16)) register_32 (.D(undriven_32), .en(load), .clk(load), .Q(S59), .clr(reset));
  Multiplexer #(.select(6), .width(16)) multiplexer_1 (
    .in0(S0), .in1(S1), .in2(S2), .in3(S3), .in4(S4), .in5(S5), .in6(S6), .in7(S7), .in8(S8), .in9(S9),
    .in10(S10), .in11(S11), .in12(S12), .in13(S13), .in14(S14), .in15(S15), .in16(S16), .in17(S17),
    .in18(S18), .in19(S19), .in20(S20), .in21(S21), .in22(S22), .in23(S23), .in24(S24), .in25(S25),
    .in26(S26), .in27(S27), .in28(S28), .in29(S29), .in30(S30), .in31(S31), .in32(S32), .in33(S33),
    .in34(S34), .in35(S35), .in36(S36), .in37(S37), .in38(S38), .in39(S39), .in40(S40), .in41(S41),
    .in42(S42), .in43(S43), .in44(S44), .in45(S45), .in46(S46), .in47(S47), .in48(S48), .in49(S49),
    .in50(S50), .in51(S51), .in52(S52), .in53(S53), .in54(S54), .in55(S55), .in56(S56), .in57(S57),
    .in58(S58), .in59(S59), .in60(S60), .in61(S61), .in62(S62), .in63(S63), .out(output_code), .sel(value_clk));
  // DipSwitch #(.number(16)) dipswitch_33: pin names not known
  Register #(.width(16)) register_33 (.D(undriven_33), .en(load), .clk(load), .Q(S4), .clr(reset));
  // DipSwitch #(.number(16)) dipswitch_34: pin names not known
  Register #(.width(16)) register_34 (.D(undriven_34), .en(load), .clk(load), .Q(S12), .clr(reset));
  // DipSwitch #(.number(16)) dipswitch_35: pin names not known
  Register #(.width(16)) register_35 (.D(undriven_35), .en(load), .clk(load), .Q(S20), .clr(reset));
  // DipSwitch #(.number(16)) dipswitch_36: pin names not known
  Register #(.width(16)) register_36 (.D(undriven_36), .en(load), .clk(load), .Q(S28), .clr(reset));
  // DipSwitch #(.number(16)) dipswitch_37: pin names not known
  Register #(.width(16)) register_37 (.D(undriven_37), .en(load), .clk(load), .Q(S36), .clr(reset));
  // DipSwitch #(.number(16)) dipswitch_38: pin names not known
  Register #(.width(16)) register_38 (.D(undriven_38), .en(load), .clk(load), .Q(S44), .clr(reset));
  // DipSwitch #(.number(16)) dipswitch_39: pin names not known
  Register #(.width(16)) register_39 (.D(undriven_39), .en(load), .clk(load), .Q(S52), .clr(reset));
  // DipSwitch #(.number(16)) dipswitch_40: pin names not known
  Register #(.width(16)) register_40 (.D(undriven_40), .en(load), .clk(load), .Q(S60), .clr(reset));
  // DipSwitch #(.number(16)) dipswitch_41: pin names not known
  Register #(.width(16)) register_41 (.D(undriven_41), .en(load), .clk(load), .Q(S5), .clr(reset));
  // DipSwitch #(.number(16)) dipswitch_42: pin names not known
  Register #(.width(16)) register_42 (.D(undriven_42), .en(load), .clk(load), .Q(S13), .clr(reset));
  // DipSwitch #(.number(16)) dipswitch_43: pin names not known
  Register #(.width(16)) register_43 (.D(undriven_43), .en(load), .clk(load), .Q(S21), .clr(reset));
  // DipSwitch #(.number(16)) dipswitch_44: pin names not known
  Register #(.width(16)) register_44 (.D(undriven_44), .en(load), .clk(load), .Q(S29), .clr(reset));
  // DipSwitch #(.number(16)) dipswitch_45: pin names not known
  Register #(.width(16)) register_45 (.D(undriven_45), .en(load), .clk(load), .Q(S37), .clr(reset));
  // DipSwitch #(.number(16)) dipswitch_46: pin names not known
  Register #(.width(16)) register_46 (.D(undriven_46), .en(load), .clk(load), .Q(S45), .clr(reset));
  // DipSwitch #(.number(16)) dipswitch_47: pin names not known
  Register #(.width(16)) register_47 (.D(undriven_47), .en(load), .clk(load), .Q(S53), .clr(reset));
  // DipSwitch #(.number(16)) dipswitch_48: pin names not known
  Register #(.width(16)) register_48 (.D(undriven_48), .en(load), .clk(load), .Q(S61), .clr(reset));
  // DipSwitch #(.number(16)) dipswitch_49: pin names not known
  Register #(.width(16)) register_49 (.D(undriven_49), .en(load), .clk(load), .Q(S6), .clr(reset));
  // DipSwitch #(.number(16)) dipswitch_50: pin names not known
  Register #(.width(16)) register_50 (.D(undriven_50), .en(load), .clk(load), .Q(S14), .clr(reset));
  // DipSwitch #(.number(16)) dipswitch_51: pin names not known
  Register #(.width(16)) register_51 (.D(undriven_51), .en(load), .clk(load), .Q(S22), .clr(reset));
  // DipSwitch #(.number(16)) dipswitch_52: pin names not known
  Register #(.width(16)) register_52 (.D(undriven_52), .en(load), .clk(load), .Q(S30), .clr(reset));
  // DipSwitch #(.number(16)) dipswitch_53: pin names not known
  // DipSwitch #(.number(16)) dipswitch_54: pin names not known
  // DipSwitch #(.number(16)) dipswitch_55: pin names not known
  // DipSwitch #(.number(16)) dipswitch_56: pin names not known
  Register #(.width(16)) register_53 (.D(undriven_53), .en(load), .clk(load), .Q(S38), .clr(reset));
  Register #(.width(16)) register_54 (.D(undriven_54), .en(load), .clk(load), .Q(S46), .clr(reset));
  Register #(.width(16)) register_55 (.D(undriven_55), .en(load), .clk(load), .Q(S54), .clr(reset));
  Register #(.width(16)) register_56 (.D(undriven_56), .en(load), .clk(load), .Q(S62), .clr(reset));
  // DipSwitch #(.number(16)) dipswitch_57: pin names not known
  // DipSwitch #(.number(16)) dipswitch_58: pin names not known
  // DipSwitch #(.number(16)) dipswitch_59: pin names not known
  // DipSwitch #(.number(16)) dipswitch_60: pin names not known
  Register #(.width(16)) register_57 (.D(undriven_57), .en(load), .clk(load), .Q(S7), .clr(reset));
  Register #(.width(16)) register_58 (.D(undriven_58), .en(load), .clk(load), .Q(S15), .clr(reset));
  Register #(.width(16)) register_59 (.D(undriven_59), .en(load), .clk(load), .Q(S23), .clr(reset));
  Register #(.width(16)) register_60 (.D(undriven_60), .en(load), .clk(load), .Q(S31), .clr(reset));
  // DipSwitch #(.number(16)) dipswitch_61: pin names not known
  Register #(.width(16)) register_61 (.D(undriven_61), .en(load), .clk(load), .Q(S39), .clr(reset));
  // DipSwitch #(.number(16)) dipswitch_62: pin names not known
  Register #(.width(16)) register_62 (.D(undriven_62), .en(load), .clk(load), .Q(S47), .clr(reset));
  // DipSwitch #(.number(16)) dipswitch_63: pin names not known
  Register #(.width(16)) register_63 (.D(undriven_63), .en(load), .clk(load), .Q(S55), .clr(reset));
  // DipSwitch #(.number(16)) dipswitch_64: pin names not known
  Register #(.width(16)) register_64 (.D(undriven_64), .en(load), .clk(load), .Q(S63), .clr(reset));
endmodule
