// Logisim project decodeur_decimal.circ as structural Verilog
module main (
);

  wire dec7_1_a, dec7_1_b, dec7_1_c, dec7_1_d, dec7_1_e, dec7_1_f, dec7_1_g;
  wire [3:0] binary_to_bcd_converter_1_p2, binary_to_bcd_converter_1_p3, binary_to_bcd_converter_1_p4;
  wire [7:0] binary_to_bcd_converter_1_p1;

  // DipSwitch dipswitch_1: pin names not known
  Hex_Digit_Display hex_digit_display_1 (.value(binary_to_bcd_converter_1_p2));  // open: dp
  Hex_Digit_Display hex_digit_display_2 (.value(binary_to_bcd_converter_1_p3));  // open: dp
  // Binary_to_BCD_converter #(.binvalue(8)) binary_to_bcd_converter_1: pin names not known; wires that end beside it: binary_to_bcd_converter_1_p1, binary_to_bcd_converter_1_p2, binary_to_bcd_converter_1_p3, binary_to_bcd_converter_1_p4
  Hex_Digit_Display hex_digit_display_3 (.value(binary_to_bcd_converter_1_p4));  // open: dp
  _7_Segment_Display u_7_segment_display_1 (
    .g(dec7_1_g), .f(dec7_1_f), .a(dec7_1_a), .b(dec7_1_b), .e(dec7_1_e), .d(dec7_1_d), .c(dec7_1_c));  // open: dp
  dec7 dec7_1 (
    .in_1(binary_to_bcd_converter_1_p4), .b(dec7_1_b), .c(dec7_1_c), .d(dec7_1_d), .e(dec7_1_e),
    .f(dec7_1_f), .g(dec7_1_g), .a(dec7_1_a));
endmodule

module dec7 (
  input  [3:0] in_1,
  output a,
  output b,
  output c,
  output d,
  output e,
  output f,
  output g
);

  wire and_1_out, and_2_out, and_3_out, and_4_out, and_5_out, and_6_out, and_7_out, and_8_out, and_9_out,
       and_10_out, and_11_out, and_12_out, and_13_out, and_14_out, and_15_out, and_16_out, and_17_out,
       and_18_out, and_19_out, and_20_out, and_21_out, and_22_out, and_23_out, and_24_out, and_25_out,
       and_26_out, and_27_out, and_28_out, and_29_out, and_30_out, and_31_out, and_32_out, and_33_out,
       and_34_out, and_35_out, not_1_out, not_2_out, not_3_out, not_4_out;

  not not_1 (not_1_out, in_1[3]);
  not not_2 (not_2_out, in_1[2]);
  not not_3 (not_3_out, in_1[1]);
  not not_4 (not_4_out, in_1[0]);
  and and_1 (and_1_out, not_2_out, not_4_out);
  and and_2 (and_2_out, not_1_out, in_1[1]);
  and and_3 (and_3_out, not_1_out, in_1[2], in_1[0]);
  and and_4 (and_4_out, in_1[3], not_2_out, not_3_out);
  and and_5 (and_5_out, in_1[3], not_4_out);
  and and_6 (and_6_out, in_1[2], in_1[1]);
  and and_7 (and_7_out, not_1_out, not_3_out, not_4_out);
  and and_8 (and_8_out, not_1_out, in_1[1], in_1[0]);
  and and_9 (and_9_out, not_2_out, not_4_out);
  and and_10 (and_10_out, in_1[3], not_3_out, in_1[0]);
  and and_11 (and_11_out, not_1_out, not_2_out);
  and and_12 (and_12_out, not_1_out, in_1[2]);
  and and_13 (and_13_out, in_1[3], not_2_out);
  and and_14 (and_14_out, not_3_out, in_1[0]);
  and and_15 (and_15_out, not_2_out, not_3_out);
  and and_16 (and_16_out, not_2_out, in_1[0]);
  and and_17 (and_17_out, in_1[2], not_3_out, in_1[0]);
  and and_18 (and_18_out, not_2_out, in_1[1], in_1[0]);
  and and_19 (and_19_out, not_1_out, not_2_out, not_4_out);
  and and_20 (and_20_out, in_1[3], not_3_out, not_4_out);
  and and_21 (and_21_out, in_1[2], in_1[1], not_4_out);
  and and_22 (and_22_out, not_2_out, not_4_out);
  and and_23 (and_23_out, in_1[1], not_4_out);
  and and_24 (and_24_out, in_1[3], in_1[1]);
  and and_25 (and_25_out, in_1[3], in_1[2]);
  and and_26 (and_26_out, not_3_out, not_4_out);
  and and_27 (and_27_out, not_1_out, in_1[2], not_3_out);
  and and_28 (and_28_out, in_1[2], not_4_out);
  and and_29 (and_29_out, in_1[3], not_2_out);
  and and_30 (and_30_out, in_1[3], in_1[1]);
  and and_31 (and_31_out, not_2_out, in_1[1]);
  and and_32 (and_32_out, in_1[3], not_2_out);
  and and_33 (and_33_out, not_1_out, in_1[2], not_3_out);
  and and_34 (and_34_out, in_1[1], not_4_out);
  and and_35 (and_35_out, in_1[3], in_1[0]);
  or or_1 (a, and_1_out, and_2_out, and_3_out, and_4_out, and_5_out, and_6_out);
  or or_2 (b, and_7_out, and_8_out, and_9_out, and_10_out, and_11_out);
  or or_3 (c, and_12_out, and_13_out, and_14_out, and_15_out, and_16_out);
  or or_4 (d, and_17_out, and_18_out, and_19_out, and_20_out, and_21_out);
  or or_5 (e, and_22_out, and_23_out, and_24_out, and_25_out);
  or or_6 (f, and_26_out, and_27_out, and_28_out, and_29_out, and_30_out);
  or or_7 (g, and_31_out, and_32_out, and_33_out, and_34_out, and_35_out);
endmodule
